# Fritzing sketch Diagrama (saved by Fritzing 0.9.3b)
breadboards: 1

parts:
  Componente1 = Arduino Mega 2560 (Rev3)
  J1 = Basic Servo
  J2 = Basic Servo
  J3 = Basic Servo
  J5 = Basic Servo
  J6 = Basic Servo
  J7 = Basic Servo
  J4 = Basic Servo
  Power_plug1 = Power plug

nets:
  GND: Componente1.GND, J1.gnd, J2.gnd, J3.gnd, J5.gnd, J6.gnd, J7.gnd, J4.gnd, Power_plug1.GND
  N1: Componente1.D8_PWM, J7.pulse
  N2: Componente1.D2_PWM, J1.pulse
  N3: Componente1.D3_PWM, J3.pulse
  N4: Componente1.D4_PWM, J5.pulse
  N5: Componente1.D5_PWM, J6.pulse
  N6: Componente1.D6_PWM, J4.pulse
  N7: Componente1.D7_PWM, J2.pulse
  VCC: J1.vcc, J2.vcc, J3.vcc, J5.vcc, J6.vcc, J7.vcc, J4.vcc, Power_plug1.VCC

notes:
  Alimentacion Externa 5V
  Segmento A
  Segmento B
  Segmento C
  Segmento D
  Segmento F
  Segmento E
  Segmento G
